// Logisim project scrolling_display_rom.circ as structural Verilog: 1 circuit, main circuit main
module main (
);

  wire button_1_out, clock_1_out, clock_2_out;
  wire [7:0] counter_1_q, rom_1_data, shift_register_1_p5, shift_register_1_p6, shift_register_1_p7,
       shift_register_2_p4, shift_register_2_p5, shift_register_2_p6, shift_register_2_p7,
       shift_register_2_p8, shift_register_2_p10, shift_register_2_p11, shift_register_2_p12,
       shift_register_3_p4, shift_register_3_p5, shift_register_3_p6, shift_register_3_p7,
       shift_register_3_p8, shift_register_3_p10, shift_register_3_p11, shift_register_3_p12,
       shift_register_4_p4, shift_register_4_p5, shift_register_4_p6, shift_register_4_p7,
       shift_register_4_p8, shift_register_4_p10, shift_register_4_p11, shift_register_4_p12,
       shift_register_5_p4, shift_register_5_p5, shift_register_5_p6, shift_register_5_p7,
       shift_register_5_p8, shift_register_5_p9, shift_register_5_p10, shift_register_5_p11,
       shift_register_6_p4, shift_register_6_p5, shift_register_6_p6, shift_register_6_p7,
       shift_register_6_p8, shift_register_6_p9, shift_register_6_p10, shift_register_6_p11,
       shift_register_6_p12, shift_register_6_p13, shift_register_6_p14, shift_register_6_p15,
       shift_register_6_p16;

  Button button_1 (.out(button_1_out));
  Counter counter_1 (
    .clr(button_1_out), .up(1'b1), .count(1'b1), .clk(clock_1_out), .Q(counter_1_q));  // open: load, D, carry
  Clock clock_1 (.out(clock_1_out));
  ROM rom_1 (.addr(counter_1_q), .data(rom_1_data));
  Clock clock_2 (.out(clock_2_out));
  // Shift_Register #(.width(8)) shift_register_1: pin names not known; wires that end beside it: button_1_out, 1'b1, clock_2_out, rom_1_data, shift_register_1_p5, shift_register_1_p6, shift_register_1_p7
  // Shift_Register #(.width(8)) shift_register_2: pin names not known; wires that end beside it: button_1_out, 1'b1, clock_2_out, shift_register_2_p4, shift_register_2_p5, shift_register_2_p6, shift_register_2_p7, shift_register_2_p8, shift_register_2_p4, shift_register_2_p10, shift_register_2_p11, shift_register_2_p12
  // Shift_Register #(.width(8)) shift_register_3: pin names not known; wires that end beside it: button_1_out, 1'b1, clock_2_out, shift_register_3_p4, shift_register_3_p5, shift_register_3_p6, shift_register_3_p7, shift_register_3_p8, shift_register_3_p4, shift_register_3_p10, shift_register_3_p11, shift_register_3_p12
  // Shift_Register #(.width(8)) shift_register_4: pin names not known; wires that end beside it: button_1_out, 1'b1, clock_2_out, shift_register_4_p4, shift_register_4_p5, shift_register_4_p6, shift_register_4_p7, shift_register_4_p8, shift_register_4_p4, shift_register_4_p10, shift_register_4_p11, shift_register_4_p12
  // Shift_Register #(.width(8)) shift_register_5: pin names not known; wires that end beside it: button_1_out, 1'b1, clock_2_out, shift_register_5_p4, shift_register_5_p5, shift_register_5_p6, shift_register_5_p7, shift_register_5_p8, shift_register_5_p9, shift_register_5_p10, shift_register_5_p11
  // Shift_Register #(.width(8)) shift_register_6: pin names not known; wires that end beside it: button_1_out, 1'b1, clock_2_out, shift_register_6_p4, shift_register_6_p5, shift_register_6_p6, shift_register_6_p7, shift_register_6_p8, shift_register_6_p9, shift_register_6_p10, shift_register_6_p11, shift_register_6_p12, shift_register_6_p13, shift_register_6_p14, shift_register_6_p15, shift_register_6_p16
  DotMatrix #(.matrixcols(8), .matrixrows(8)) dotmatrix_1 (
    .col0(shift_register_6_p16), .col1(shift_register_6_p15), .col2(shift_register_6_p14),
    .col3(shift_register_6_p13), .col4(shift_register_6_p12), .col5(shift_register_6_p11),
    .col6(shift_register_6_p10), .col7(shift_register_6_p9));
  DotMatrix #(.matrixcols(8), .matrixrows(8)) dotmatrix_2 (
    .col0(shift_register_6_p4), .col1(shift_register_6_p8), .col2(shift_register_6_p7),
    .col3(shift_register_6_p6), .col4(shift_register_6_p5), .col5(shift_register_5_p11),
    .col6(shift_register_5_p10), .col7(shift_register_5_p9));
  DotMatrix #(.matrixcols(8), .matrixrows(8)) dotmatrix_3 (
    .col0(shift_register_5_p4), .col1(shift_register_5_p8), .col2(shift_register_5_p7),
    .col3(shift_register_5_p6), .col4(shift_register_5_p5), .col5(shift_register_4_p12),
    .col6(shift_register_4_p11), .col7(shift_register_4_p10));
  DotMatrix #(.matrixcols(8), .matrixrows(8)) dotmatrix_4 (
    .col0(shift_register_4_p4), .col1(shift_register_4_p8), .col2(shift_register_4_p7),
    .col3(shift_register_4_p6), .col4(shift_register_4_p5), .col5(shift_register_3_p12),
    .col6(shift_register_3_p11), .col7(shift_register_3_p10));
  DotMatrix #(.matrixcols(8), .matrixrows(8)) dotmatrix_5 (
    .col0(shift_register_3_p4), .col1(shift_register_3_p8), .col2(shift_register_3_p7),
    .col3(shift_register_3_p6), .col4(shift_register_3_p5), .col5(shift_register_2_p12),
    .col6(shift_register_2_p11), .col7(shift_register_2_p10));
  DotMatrix #(.matrixcols(8), .matrixrows(8)) dotmatrix_6 (
    .col0(shift_register_2_p4), .col1(shift_register_2_p8), .col2(shift_register_2_p7),
    .col3(shift_register_2_p6), .col4(shift_register_2_p5), .col5(shift_register_1_p7),
    .col6(shift_register_1_p6), .col7(shift_register_1_p5));

  // Notes on the sheet:
  //   contents of rom_1 (hex, n*v repeats v):
  //   38 44 22 44 38
endmodule
